# Fritzing sketch IoT1929 (saved by Fritzing 0.9.3b)
breadboards: 1

parts:
  Parça1 = Arduino Uno (Rev3)
  R1 = Rotary Potentiometer (Small) [maximum_resistance=100kΩ package=THT]
  LED1 = smd LED [color="Green (570nm)" package="0603 [SMD]"]
  LED2 = smd LED [color="Red (633nm)" package="0603 [SMD]"]
  LED3 = smd LED [color="Blue (525nm)" package="0603 [SMD]"]
  R2 = Resistor [tolerance=±5% resistance=220 package="0805 [SMD]"]
  R3 = Resistor [tolerance=±5% resistance=220 package="0805 [SMD]"]
  R4 = Resistor [tolerance=±5% resistance=220 package="0805 [SMD]"]
  LCD1 = LCD screen
  Parça4 = FC-28 Soil Hygrometer Module - Probe
  Parça5 = FC-28 Soil Hygrometer Module

nets:
  N1: Parça1.A0, Parça5.AO
  N2: Parça1.D11_PWM/MOSI, LCD1.E
  N3: Parça1.D12/MISO, LCD1.RS
  N4: Parça1.D2, LCD1.DB7
  N5: Parça1.D3_PWM, LCD1.DB6
  N6: Parça1.D4, LCD1.DB5
  N7: Parça1.D5_PWM, LCD1.DB4
  5V: Parça1.5V, R1.leg1, Parça5.VCC
  GND: Parça1.GND, R1.leg2, LED1.anode, LED2.anode, LED3.anode, Parça5.GND
  N8: R1.wiper, LCD1.V0
  N9: LED1.cathode, R2.Pin_1
  N10: LED2.cathode, R3.Pin_1
  N11: LED3.cathode, R4.Pin_1
  N12: LCD1.VSS, LCD1.R/W, LCD1.LED+, LCD1.LED-
  N13: Parça4.POS, Parça5.POS
  N14: Parça4.NEG, Parça5.NEG

custom parts:
  FC-28 Soil Hygrometer Module - Probe: The FC-28 is a soil hygrometer module that uses the Texas Instruments LM393 comparator chip to provide an analog measurement of soil humidity.
  FC-28 Soil Hygrometer Module: The FC-28 is a soil hygrometer module that uses the Texas Instruments LM393 comparator chip to provide an analog measurement of soil humidity. The digital output is high when soil moisture is over a certain threshold, as determined by adjusting the potentiometer.
